// Logisim project Microprocessor.circ as structural Verilog: 17 circuits, main circuit MUX_4to1
module MUX_4to1 (
  input  E3,
  input  E2,
  input  E1,
  input  E0,
  input  C1,
  input  C0,
  output S
);

  wire and_1_out, and_2_out, and_3_out, and_4_out, not_1_out, not_2_out;

  not not_1 (not_1_out, C1);
  not not_2 (not_2_out, C0);
  and and_1 (and_1_out, C1, E3, C0);
  and and_2 (and_2_out, not_1_out, E2, C0);
  and and_3 (and_3_out, C1, E1, not_2_out);
  and and_4 (and_4_out, not_1_out, E0, not_2_out);
  or or_1 (S, and_1_out, and_2_out, and_3_out, and_4_out);
endmodule

module MUX8_4to1 (
  input  [7:0] E0,
  input  [7:0] E1,
  input  [7:0] E2,
  input  [7:0] E3,
  input  C1,
  input  C0,
  output [7:0] S
);

  MUX_4to1 mux_4to1_1 (.E3(E3[0]), .E2(E2[0]), .E1(E1[0]), .E0(E0[0]), .C1(C1), .C0(C0), .S(S[0]));
  MUX_4to1 mux_4to1_2 (.E3(E3[1]), .E2(E2[1]), .E1(E1[1]), .E0(E0[1]), .C1(C1), .C0(C0), .S(S[1]));
  MUX_4to1 mux_4to1_3 (.E3(E3[2]), .E2(E2[2]), .E1(E1[2]), .E0(E0[2]), .C1(C1), .C0(C0), .S(S[2]));
  MUX_4to1 mux_4to1_4 (.E3(E3[3]), .E2(E2[3]), .E1(E1[3]), .E0(E0[3]), .C1(C1), .C0(C0), .S(S[3]));
  MUX_4to1 mux_4to1_5 (.E3(E3[4]), .E2(E2[4]), .E1(E1[4]), .E0(E0[4]), .C1(C1), .C0(C0), .S(S[4]));
  MUX_4to1 mux_4to1_6 (.E3(E3[5]), .E2(E2[5]), .E1(E1[5]), .E0(E0[5]), .C1(C1), .C0(C0), .S(S[5]));
  MUX_4to1 mux_4to1_7 (.E3(E3[6]), .E2(E2[6]), .E1(E1[6]), .E0(E0[6]), .C1(C1), .C0(C0), .S(S[6]));
  MUX_4to1 mux_4to1_8 (.E3(E3[7]), .E2(E2[7]), .E1(E1[7]), .E0(E0[7]), .C1(C1), .C0(C0), .S(S[7]));
endmodule

module ADD1 (
  input  A,
  input  B,
  input  Re,
  output S,
  output Rs
);

  wire and_1_out, and_2_out, and_3_out, or_1_out, xor_2_out;

  xor xor_1 (S, B, xor_2_out);
  xor xor_2 (xor_2_out, A, Re);
  and and_1 (and_1_out, A, B);
  or or_1 (or_1_out, and_1_out, and_2_out);
  or or_2 (Rs, or_1_out, and_3_out);
  and and_2 (and_2_out, A, Re);
  and and_3 (and_3_out, B, Re);
endmodule

module ADD8 (
  input  [7:0] A,
  input  [7:0] B,
  input  Re,
  output Rs,
  output [7:0] S
);

  wire add1_2_rs, add1_3_rs, add1_4_rs, add1_5_rs, add1_6_rs, add1_7_rs, add1_8_rs;

  ADD1 add1_1 (.A(A[7]), .B(B[7]), .Re(add1_2_rs), .S(S[7]), .Rs(Rs));
  ADD1 add1_2 (.A(A[6]), .B(B[6]), .Re(add1_3_rs), .S(S[6]), .Rs(add1_2_rs));
  ADD1 add1_3 (.A(A[5]), .B(B[5]), .Re(add1_4_rs), .S(S[5]), .Rs(add1_3_rs));
  ADD1 add1_4 (.A(A[4]), .B(B[4]), .Re(add1_5_rs), .S(S[4]), .Rs(add1_4_rs));
  ADD1 add1_5 (.A(A[3]), .B(B[3]), .Re(add1_6_rs), .S(S[3]), .Rs(add1_5_rs));
  ADD1 add1_6 (.A(A[2]), .B(B[2]), .Re(add1_7_rs), .S(S[2]), .Rs(add1_6_rs));
  ADD1 add1_7 (.A(A[1]), .B(B[1]), .Re(add1_8_rs), .S(S[1]), .Rs(add1_7_rs));
  ADD1 add1_8 (.A(A[0]), .B(B[0]), .Re(Re), .S(S[0]), .Rs(add1_8_rs));
endmodule

module SUB8 (
  input  [7:0] A,
  input  [7:0] B,
  output [7:0] R
);

  wire [7:0] not_1_out;

  ADD8 add8_1 (.Re(1'b1), .A(A), .B(not_1_out), .S(R));  // open: Rs
  assign not_1_out = ~B;  // NOT_Gate not_1, 8 bits wide
endmodule

module ALU (
  input  [7:0] B,
  input  [7:0] A,
  input  [1:0] Op,
  output [7:0] R
);

  wire [7:0] add8_1_s, and_1_out, sub8_1_r;

  assign and_1_out = B & A;  // AND_Gate and_1, 8 bits wide
  SUB8 sub8_1 (.A(A), .B(B), .R(sub8_1_r));
  ADD8 add8_1 (.A(A), .B(B), .S(add8_1_s));  // open: Re, Rs
  MUX8_4to1 mux8_4to1_1 (.E0(add8_1_s), .E1(sub8_1_r), .E2(and_1_out), .E3(B), .C0(Op[0]), .C1(Op[1]), .S(R));
endmodule

module DEC_3_8 (
  input  E2,
  input  E1,
  input  E0,
  output S0,
  output S1,
  output S2,
  output S3,
  output S4,
  output S5,
  output S6,
  output S7
);

  wire not_1_out, not_2_out, not_3_out;

  not not_1 (not_1_out, E1);
  not not_2 (not_2_out, E2);
  not not_3 (not_3_out, E0);
  and and_1 (S0, not_2_out, not_1_out, not_3_out);
  and and_2 (S1, not_2_out, not_1_out, E0);
  and and_3 (S2, not_2_out, E1, not_3_out);
  and and_4 (S3, not_2_out, E1, E0);
  and and_5 (S4, E2, not_1_out, not_3_out);
  and and_6 (S5, E2, not_1_out, E0);
  and and_7 (S6, E2, E1, not_3_out);
  and and_8 (S7, E2, E1, E0);
endmodule

module REG1 (
  input  IN,
  input  WR,
  input  CLK,
  input  INIT,
  output OUT
);

  wire multiplexer_1_out;

  Multiplexer multiplexer_1 (.in0(IN), .in1(OUT), .out(multiplexer_1_out), .sel(WR));
  D_Flip_Flop d_ff_1 (.D(multiplexer_1_out), .clk(CLK), .Q(OUT), .preset(1'b0), .reset(INIT));  // open: Qn
endmodule

module REG8 (
  input  [7:0] IN,
  input  WR,
  input  CLK,
  input  INIT,
  output [7:0] OUT
);

  REG1 reg1_1 (.WR(WR), .INIT(INIT), .IN(IN[7]), .CLK(CLK), .OUT(CLK));
  REG1 reg1_2 (.WR(WR), .INIT(INIT), .IN(IN[6]), .CLK(CLK), .OUT(CLK));
  REG1 reg1_3 (.WR(WR), .INIT(INIT), .IN(IN[5]), .CLK(CLK), .OUT(CLK));
  REG1 reg1_4 (.WR(WR), .INIT(INIT), .IN(IN[4]), .CLK(CLK), .OUT(CLK));
  REG1 reg1_5 (.WR(WR), .INIT(INIT), .IN(IN[3]), .CLK(CLK), .OUT(CLK));
  REG1 reg1_6 (.WR(WR), .INIT(INIT), .IN(IN[2]), .CLK(CLK), .OUT(CLK));
  REG1 reg1_7 (.WR(WR), .INIT(INIT), .IN(IN[1]), .CLK(CLK), .OUT(CLK));
  REG1 reg1_8 (.WR(WR), .INIT(INIT), .IN(IN[0]), .CLK(CLK), .OUT(OUT[0]));

  assign OUT[7:1] = {7{CLK}};
endmodule

module GATE8 (
  input  [7:0] IN,
  input  in_2,
  output [7:0] OUT
);

  assign OUT = in_2 ? IN : 8'bz;  // Controlled_Buffer controlled_buffer_1
endmodule

module REGBANK (
  input  [7:0] IN,
  input  [2:0] N1,
  input  [2:0] N0,
  input  WR,
  input  CLK,
  input  INIT,
  output [7:0] OUT1,
  output [7:0] OUT0
);

  wire dec_3_8_1_s0, dec_3_8_1_s1, dec_3_8_1_s2, dec_3_8_1_s3, dec_3_8_1_s4, dec_3_8_1_s5, dec_3_8_1_s6,
       dec_3_8_1_s7, dec_3_8_2_s0, dec_3_8_2_s1, dec_3_8_2_s2, dec_3_8_2_s3, dec_3_8_2_s4, dec_3_8_2_s5,
       dec_3_8_2_s6, dec_3_8_2_s7, demultiplexer_1_out0, demultiplexer_1_out1, demultiplexer_1_out2,
       demultiplexer_1_out3, demultiplexer_1_out4, demultiplexer_1_out5, demultiplexer_1_out6,
       demultiplexer_1_out7;
  wire [7:0] reg8_1_out, reg8_2_out, reg8_3_out, reg8_4_out, reg8_5_out, reg8_6_out, reg8_7_out, reg8_8_out;

  Demultiplexer #(.select(3)) demultiplexer_1 (
    .out0(demultiplexer_1_out0), .out1(demultiplexer_1_out1), .out2(demultiplexer_1_out2),
    .out3(demultiplexer_1_out3), .out4(demultiplexer_1_out4), .out5(demultiplexer_1_out5),
    .out6(demultiplexer_1_out6), .out7(demultiplexer_1_out7), .in(WR), .sel(N0));
  DEC_3_8 dec_3_8_1 (
    .E2(N0[0]), .E1(N0[1]), .E0(N0[2]), .S1(dec_3_8_1_s1), .S2(dec_3_8_1_s2), .S3(dec_3_8_1_s3),
    .S4(dec_3_8_1_s4), .S5(dec_3_8_1_s5), .S6(dec_3_8_1_s6), .S7(dec_3_8_1_s7), .S0(dec_3_8_1_s0));
  REG8 reg8_1 (.WR(demultiplexer_1_out0), .CLK(CLK), .INIT(INIT), .IN(IN), .OUT(reg8_1_out));
  REG8 reg8_2 (.WR(demultiplexer_1_out1), .CLK(CLK), .INIT(INIT), .IN(IN), .OUT(reg8_2_out));
  REG8 reg8_3 (.WR(demultiplexer_1_out2), .CLK(CLK), .INIT(INIT), .IN(IN), .OUT(reg8_3_out));
  REG8 reg8_4 (.WR(demultiplexer_1_out3), .CLK(CLK), .INIT(INIT), .IN(IN), .OUT(reg8_4_out));
  REG8 reg8_5 (.WR(demultiplexer_1_out4), .CLK(CLK), .INIT(INIT), .IN(IN), .OUT(reg8_5_out));
  REG8 reg8_6 (.WR(demultiplexer_1_out5), .CLK(CLK), .INIT(INIT), .IN(IN), .OUT(reg8_6_out));
  REG8 reg8_7 (.WR(demultiplexer_1_out6), .CLK(CLK), .INIT(INIT), .OUT(reg8_7_out));  // open: IN
  REG8 reg8_8 (.WR(demultiplexer_1_out7), .CLK(CLK), .INIT(INIT), .IN(IN), .OUT(reg8_8_out));
  GATE8 gate8_1 (.IN(reg8_1_out), .in_2(dec_3_8_1_s0), .OUT(OUT0));
  GATE8 gate8_2 (.IN(reg8_2_out), .in_2(dec_3_8_1_s1), .OUT(OUT0));
  GATE8 gate8_3 (.IN(reg8_3_out), .in_2(dec_3_8_1_s2), .OUT(OUT0));
  GATE8 gate8_4 (.IN(reg8_4_out), .in_2(dec_3_8_1_s3), .OUT(OUT0));
  GATE8 gate8_5 (.IN(reg8_5_out), .in_2(dec_3_8_1_s4), .OUT(OUT0));
  GATE8 gate8_6 (.IN(reg8_6_out), .in_2(dec_3_8_1_s5), .OUT(OUT0));
  GATE8 gate8_7 (.IN(reg8_7_out), .in_2(dec_3_8_1_s6), .OUT(OUT0));
  GATE8 gate8_8 (.IN(reg8_8_out), .in_2(dec_3_8_1_s7), .OUT(OUT0));
  GATE8 gate8_9 (.IN(reg8_1_out), .in_2(dec_3_8_2_s0), .OUT(OUT1));
  GATE8 gate8_10 (.IN(reg8_2_out), .in_2(dec_3_8_2_s1), .OUT(OUT1));
  GATE8 gate8_11 (.IN(reg8_3_out), .in_2(dec_3_8_2_s2), .OUT(OUT1));
  GATE8 gate8_12 (.IN(reg8_4_out), .in_2(dec_3_8_2_s3), .OUT(OUT1));
  GATE8 gate8_13 (.IN(reg8_5_out), .in_2(dec_3_8_2_s4), .OUT(OUT1));
  GATE8 gate8_14 (.IN(reg8_6_out), .in_2(dec_3_8_2_s5), .OUT(OUT1));
  GATE8 gate8_15 (.IN(reg8_7_out), .in_2(dec_3_8_2_s6), .OUT(OUT1));
  GATE8 gate8_16 (.IN(reg8_8_out), .in_2(dec_3_8_2_s7), .OUT(OUT1));
  DEC_3_8 dec_3_8_2 (
    .E2(N1[0]), .E1(N1[1]), .E0(N1[2]), .S1(dec_3_8_2_s1), .S2(dec_3_8_2_s2), .S3(dec_3_8_2_s3),
    .S4(dec_3_8_2_s4), .S5(dec_3_8_2_s5), .S6(dec_3_8_2_s6), .S7(dec_3_8_2_s7), .S0(dec_3_8_2_s0));
endmodule

module MUX8_2to1 (
  input  [7:0] E1,
  input  [7:0] E0,
  input  C,
  output [7:0] out_4
);

  wire and_1_out, and_2_out, and_3_out, and_4_out, and_5_out, and_6_out, and_7_out, and_8_out, and_9_out,
       and_10_out, and_11_out, and_12_out, and_13_out, and_14_out, and_15_out, and_16_out, not_1_out;

  not not_1 (not_1_out, C);
  and and_1 (and_1_out, E1[0], C);
  and and_2 (and_2_out, E0[0], not_1_out);
  and and_3 (and_3_out, E1[1], C);
  and and_4 (and_4_out, E0[1], not_1_out);
  and and_5 (and_5_out, E1[2], C);
  and and_6 (and_6_out, E0[2], not_1_out);
  and and_7 (and_7_out, E1[3], C);
  and and_8 (and_8_out, E0[3], not_1_out);
  and and_9 (and_9_out, E1[4], C);
  and and_10 (and_10_out, E0[4], not_1_out);
  and and_11 (and_11_out, E1[5], C);
  and and_12 (and_12_out, E0[5], not_1_out);
  and and_13 (and_13_out, E1[6], C);
  and and_14 (and_14_out, E0[6], not_1_out);
  and and_15 (and_15_out, E1[7], C);
  and and_16 (and_16_out, E0[7], not_1_out);
  or or_1 (out_4[0], and_1_out, and_2_out);
  or or_2 (out_4[1], and_3_out, and_4_out);
  or or_3 (out_4[2], and_5_out, and_6_out);
  or or_4 (out_4[3], and_7_out, and_8_out);
  or or_5 (out_4[4], and_9_out, and_10_out);
  or or_6 (out_4[5], and_11_out, and_12_out);
  or or_7 (out_4[6], and_13_out, and_14_out);
  or or_8 (out_4[7], and_15_out, and_16_out);
endmodule

module CORE0 (
  input  WR,
  input  CLK,
  input  INIT,
  input  [2:0] N0,
  input  [1:0] OP,
  input  [2:0] N1,
  output [7:0] B,
  output [7:0] A,
  output [7:0] R
);

  wire and_1_out;
  wire [7:0] regbank_1_out1;

  REGBANK regbank_1 (.N0(N0), .IN(R), .WR(WR), .CLK(CLK), .INIT(INIT), .N1(N1), .OUT1(regbank_1_out1), .OUT0(A));
  and and_1 (and_1_out, OP[0], OP[1]);
  Multiplexer #(.width(8)) multiplexer_1 (.in0(regbank_1_out1), .in1({{5{1'b0}}, N1}), .out(B), .sel(and_1_out));
  ALU alu_1 (.B(B), .A(A), .Op(OP), .R(R));
endmodule

module SEQ (
  input  CLK,
  input  INIT,
  output BWR,
  output IWR
);

  D_Flip_Flop d_ff_1 (.D(BWR), .clk(CLK), .Q(IWR), .preset(INIT));  // open: Qn, reset
  D_Flip_Flop d_ff_2 (.D(IWR), .clk(CLK), .Q(BWR), .reset(INIT));  // open: Qn, preset
endmodule

module CORE1 (
  input  CLK,
  input  INIT
);

  wire seq_1_bwr, seq_1_iwr;
  wire [1:0] reg8_1_out;
  wire [2:0] reg8_1_out_2, reg8_1_out_3;
  wire [3:0] pc_1_out_4;
  wire [7:0] core0_1_a, core0_1_b, core0_1_r, rom_1_data;

  ROM #(.addrWidth(4)) rom_1 (.addr(pc_1_out_4), .data(rom_1_data));
  SEQ seq_1 (.CLK(CLK), .INIT(INIT), .BWR(seq_1_bwr), .IWR(seq_1_iwr));
  PC pc_1 (.CLK(CLK), .INIT(INIT), .WR(seq_1_iwr), .out_4(pc_1_out_4));
  // Probe on seq_1_iwr
  // Probe on reg8_1_out
  CORE0 core0_1 (
    .WR(seq_1_bwr), .CLK(CLK), .INIT(INIT), .N0(reg8_1_out_2), .N1(reg8_1_out_3), .OP(reg8_1_out),
    .B(core0_1_b), .A(core0_1_a), .R(core0_1_r));
  // Probe on reg8_1_out_3
  // Probe on reg8_1_out_2
  REG8 reg8_1 (.WR(seq_1_iwr), .CLK(CLK), .INIT(INIT), .IN(rom_1_data), .OUT({reg8_1_out_3, reg8_1_out_2, reg8_1_out}));
  // Probe on rom_1_data
  // Probe on core0_1_r
  // Probe on core0_1_a
  // Probe on core0_1_b

  // Notes on the sheet:
  //   contents of rom_1 (hex, n*v repeats v):
  //   c4 d3 2 ff 47
endmodule

module PC (
  input  WR,
  input  CLK,
  input  INIT,
  output [3:0] out_4
);

  wire and_1_out, and_2_out, and_3_out, xor_1_out, xor_2_out, xor_3_out, xor_4_out;

  xor xor_1 (xor_1_out, and_1_out, out_4[3]);
  D_Flip_Flop d_ff_1 (.D(xor_1_out), .clk(CLK), .Q(out_4[3]), .reset(INIT));  // open: Qn, preset
  and and_1 (and_1_out, out_4[2], and_2_out);
  xor xor_2 (xor_2_out, and_2_out, out_4[2]);
  D_Flip_Flop d_ff_2 (.D(xor_2_out), .clk(CLK), .Q(out_4[2]), .reset(INIT));  // open: Qn, preset
  and and_2 (and_2_out, and_3_out, out_4[1]);
  xor xor_3 (xor_3_out, and_3_out, out_4[1]);
  D_Flip_Flop d_ff_3 (.D(xor_3_out), .clk(CLK), .Q(out_4[1]), .reset(INIT));  // open: Qn, preset
  and and_3 (and_3_out, WR, out_4[0]);
  xor xor_4 (xor_4_out, out_4[0], WR);
  D_Flip_Flop d_ff_4 (.D(xor_4_out), .clk(CLK), .Q(out_4[0]), .reset(INIT));  // open: Qn, preset
endmodule

module FSM (
  input  WR,
  input  CLK,
  input  INIT,
  output [2:0] out_4
);

  wire and_1_out, and_2_out, and_3_out, not_1_out, xor_1_out, xor_2_out, xor_3_out;

  xor xor_1 (xor_1_out, and_1_out, out_4[2]);
  D_Flip_Flop d_ff_1 (.D(xor_1_out), .clk(CLK), .Q(out_4[2]), .reset(INIT));  // open: Qn, preset
  and and_1 (and_1_out, and_2_out, out_4[1]);
  xor xor_2 (xor_2_out, and_2_out, out_4[1]);
  D_Flip_Flop d_ff_2 (.D(xor_2_out), .clk(CLK), .Q(out_4[1]), .reset(INIT));  // open: Qn, preset
  and and_2 (and_2_out, WR, out_4[0]);
  xor xor_3 (xor_3_out, out_4[0], WR);
  D_Flip_Flop d_ff_3 (.D(xor_3_out), .clk(CLK), .Q(out_4[0]), .reset(INIT));  // open: Qn, preset
  and and_3 (and_3_out, not_1_out, out_4[1], out_4[2]);
  not not_1 (not_1_out, out_4[0]);
endmodule
